# Fritzing sketch 4xLED-Matrix (saved by Fritzing 0.9.2b)
breadboards: 1

parts:
  Arduino = Arduino Micro (Rev3)
  LED3 = 8x8 LED Matrix (green)
  LED4 = 8x8 LED Matrix (green)
  LED5 = 8x8 LED Matrix (green)
  LED6 = 8x8 LED Matrix (green)

nets:
  N1: Arduino.GND, LED3.-, LED4.-, LED5.-, LED6.-
  N2: Arduino.D2/SDA, LED3.D, LED4.D, LED5.D, LED6.D
  N3: Arduino.D3/SCL, LED3.C, LED4.C, LED5.C, LED6.C
  N4: Arduino.5V, LED3.+, LED4.+, LED5.+, LED6.+

notes:
  0x70
  0x71
  0x72
  0x73

custom parts:
  8x8 LED Matrix (green): 8x8 LED Matrix with I2C control (green)
