# Fritzing sketch licht-sensor (saved by Fritzing 0.9.2b)
breadboards: 1

parts:
  Arduino = Arduino Micro (Rev3)
  R1 = Photocell (LDR) [package=THT]
  R2 = Resistor [tolerance=±5% resistance=10k package=THT]

nets:
  N1: Arduino.GND, R1.pin_1
  N2: Arduino.5V, R2.Pin_0
  N3: Arduino.A3, R1.pin_0, R2.Pin_1
