# Fritzing sketch line-sensor (saved by Fritzing 0.9.2b)
breadboards: 1

parts:
  Arduino = Arduino Micro (Rev3)
  J1 = female pin header, 3 pins [form="♀ (female)"]
  J2 = female pin header, 3 pins [form="♀ (female)"]

nets:
  N1: Arduino.D2/SDA, J2.pin1
  N2: Arduino.D3/SCL, J1.pin1
