# Fritzing sketch motor-driver (saved by Fritzing 0.9.2b)
breadboards: 1

parts:
  Arduino = Arduino Micro (Rev3)
  M1 = DC Motor
  Power_plug1 = Power plug
  Q1 = NPN-Transistor [package="TO92 [THT]"]
  R1 = Resistor [tolerance=±5% resistance=4.7k package=THT]
  D1 = Rectifier Diode [part_number=1N4001 package="300 mil [THT]"]

nets:
  GND: Arduino.GND, Power_plug1.GND, Q1.E
  N1: Arduino.D8_PWM/A8, R1.Pin_0
  N2: M1.pin_1, Q1.C, D1.anode
  N3: M1.pin_2, Power_plug1.VCC, D1.cathode
  N4: Q1.B, R1.Pin_1
