# Fritzing sketch radar (saved by Fritzing 0.9.2b)
breadboards: 1

parts:
  Arduino = Arduino Micro (Rev3)
  J3 = Basic Servo
  SONAR1 = Maxbotix MaxSonar Ultrasonic Sensor

nets:
  N1: Arduino.D4_PWM/A6, J3.pulse
  GND: Arduino.GND, J3.gnd, SONAR1.GND
  5V: Arduino.5V, J3.vcc, SONAR1.+5V
  N2: Arduino.A4, SONAR1.AN

custom parts:
  Maxbotix MaxSonar Ultrasonic Sensor: Maxbotix MaxSonar Ultrasonic Sensor LV-EZ0, LV-EZ1, LV-EZ2, LV-EZ3, LV-EZ4
