# Fritzing sketch servo-pan-tilt (saved by Fritzing 0.9.2b)
breadboards: 1

parts:
  Arduino = Arduino Micro (Rev3)
  J3 = Basic Servo
  J4 = Basic Servo
  Power_plug1 = Power plug

nets:
  GND: Arduino.GND, J3.gnd, J4.gnd, Power_plug1.GND
  N1: Arduino.D4_PWM/A6, J3.pulse
  N2: Arduino.D12_PWM/A11, J4.pulse
  VCC: J3.vcc, J4.vcc, Power_plug1.VCC
