# Fritzing sketch servo (saved by Fritzing 0.9.2b)
breadboards: 1

parts:
  Arduino = Arduino Micro (Rev3)
  J3 = Basic Servo

nets:
  N1: Arduino.D4_PWM/A6, J3.pulse
  GND: Arduino.GND, J3.gnd
  5V: Arduino.5V, J3.vcc
