# Fritzing sketch spy-cam (saved by Fritzing 0.9.2b)
breadboards: 1

parts:
  Arduino = Arduino Micro (Rev3)
  MD03A1 = Dual VNH2SP30 Motor Driver [part_number=MD03A]
  M1 = DC Motor
  M2 = DC Motor
  Power_plug1 = Power plug
  Q1 = NPN-Transistor [package="TO92 [THT]"]
  Q2 = NPN-Transistor [package="TO92 [THT]"]
  R1 = Resistor [tolerance=±5% resistance=4.7k package=THT]
  R2 = Resistor [tolerance=±5% resistance=4.7k package=THT]
  R3 = Resistor [tolerance=±5% resistance=10k package=THT]
  R4 = Resistor [tolerance=±5% resistance=10k package=THT]
  J1 = Basic Servo  # not connected
  J2 = Basic Servo  # not connected
  Power_plug2 = Power plug  # not connected

nets (from the schematic view):
  N1: Arduino.D6_PWM/A7, MD03A1.PWM
  N2: Arduino.D7, MD03A1.1INa, R2.Pin_0
  N3: Arduino.D8_PWM/A8, MD03A1.2INb#142, R1.Pin_0
  N4: Arduino.D11_PWM, MD03A1.2PWM
  GND: Arduino.GND, MD03A1.GND#151, Power_plug1.GND, Q1.E, Q2.E
  N5: Arduino.5V, MD03A1.+5V_(IN), R3.Pin_1, R4.Pin_1
  N6: MD03A1.1INb, Q2.C, R3.Pin_0
  N7: MD03A1.2INb#143, Q1.C, R4.Pin_0
  N8: MD03A1.OUT_1A, M1.pin_1
  N9: MD03A1.OUT_1B, M1.pin_2
  N10: MD03A1.OUT_2A, M2.pin_1
  N11: MD03A1.OUT_2B, M2.pin_2
  VIN: MD03A1.VIN, Power_plug1.VCC
  N12: Q1.B, R1.Pin_1
  N13: Q2.B, R2.Pin_1
